// Logisim project final_logisim.circ as structural Verilog: 3 circuits, main circuit 7 segment
module main (
  input  in_1,
  input  in_2,
  input  [3:0] Passanger_Limit,
  input  in_4,
  input  in_5,
  input  in_6,
  output [3:0] out_7
);

  wire comparator_1_gt, comparator_1_lt, comparator_2_gt, enter_out, exit_out, help_1_a_2, help_1_b_2,
       help_1_c_2, help_1_d_2, help_1_e, help_1_f, help_1_g, not_1_out, not_2_out;
  wire [3:0] counter_1_q, counter_2_q, counter_3_q, counter_4_q;

  Button enter (.out(enter_out));
  Button exit (.out(exit_out));
  Counter #(.width(4), .max('hf)) counter_1 (
    .load(in_2), .Q(counter_1_q), .clk(not_1_out), .clr(in_6));  // open: D, count, carry
  not not_1 (not_1_out, enter_out);
  Counter #(.width(4), .max('hf)) counter_2 (
    .load(in_5), .Q(counter_2_q), .clk(exit_out), .clr(in_6));  // open: D, count, carry
  not not_2 (not_2_out, comparator_1_gt);
  Comparator #(.width(4)) comparator_1 (
    .a(counter_1_q), .b(counter_2_q), .gt(comparator_1_gt), .lt(comparator_1_lt));  // open: eq
  Counter #(.width(4), .max('hf)) counter_3 (
    .load(in_1), .Q(counter_3_q), .clk(not_2_out), .clr(in_6));  // open: D, count, carry
  Counter #(.width(4), .max('hf)) counter_4 (
    .load(in_4), .Q(counter_4_q), .clk(comparator_1_lt), .clr(in_6));  // open: D, count, carry
  Subtractor #(.width(4)) subtractor_1 (.a(counter_3_q), .b(counter_4_q), .out(out_7));  // open: bin, bout
  _7_segment u_7_segment_1 ();
  help help_1 (
    .D(out_7[3]), .C(out_7[2]), .B(out_7[1]), .A(out_7[0]), .a_2(help_1_a_2), .b_2(help_1_b_2),
    .c_2(help_1_c_2), .d_2(help_1_d_2), .e(help_1_e), .f(help_1_f), .g(help_1_g));
  Comparator #(.width(4)) comparator_2 (.a(out_7), .b(Passanger_Limit), .gt(comparator_2_gt));  // open: eq, lt
  _7_Segment_Display u_7_segment_display_1 (
    .g(help_1_g), .f(help_1_f), .a(help_1_a_2), .b(help_1_b_2), .e(help_1_e), .d(help_1_d_2), .c(help_1_c_2));  // open: dp
  LED led_1 (.in(comparator_2_gt));
endmodule

module _7_segment (
);
endmodule

module help (
  input  D,
  input  C,
  input  B,
  input  A,
  output a_2,
  output b_2,
  output c_2,
  output d_2,
  output e,
  output f,
  output g
);

  wire and_1_out, and_2_out, and_3_out, and_4_out, and_5_out, and_6_out, and_7_out, and_8_out, and_9_out,
       and_10_out, and_11_out, and_12_out, and_13_out, and_14_out, and_15_out, and_16_out, and_17_out,
       and_18_out, and_19_out, and_20_out, and_21_out, and_22_out, and_23_out, and_24_out, and_25_out,
       and_26_out, and_27_out, and_28_out, and_29_out, and_30_out, and_31_out, and_32_out, and_33_out,
       and_34_out, and_35_out, not_1_out, not_2_out, not_3_out, not_4_out, not_5_out, not_6_out, not_7_out,
       not_8_out, not_9_out, not_10_out, not_11_out, not_12_out, not_13_out, not_14_out, not_15_out,
       not_16_out, not_17_out, not_18_out, not_19_out, not_20_out, not_21_out, not_22_out, not_23_out,
       not_24_out, not_25_out, not_26_out, not_27_out, not_28_out, not_29_out, not_30_out, not_31_out,
       not_32_out, not_33_out, not_34_out, not_35_out, not_36_out, not_37_out, not_38_out, not_39_out,
       not_40_out, not_41_out, not_42_out, not_43_out, not_44_out;

  not not_1 (not_1_out, C);
  and and_1 (and_1_out, not_1_out, not_2_out);
  not not_2 (not_2_out, A);
  not not_3 (not_3_out, D);
  and and_2 (and_2_out, not_3_out, B);
  not not_4 (not_4_out, D);
  and and_3 (and_3_out, not_4_out, C, A);
  and and_4 (and_4_out, C, B);
  and and_5 (and_5_out, D, not_5_out, not_6_out);
  not not_5 (not_5_out, C);
  not not_6 (not_6_out, B);
  and and_6 (and_6_out, D, not_7_out);
  not not_7 (not_7_out, A);
  not not_8 (not_8_out, D);
  and and_7 (and_7_out, not_8_out, not_9_out);
  not not_9 (not_9_out, C);
  not not_10 (not_10_out, D);
  not not_11 (not_11_out, B);
  and and_8 (and_8_out, not_10_out, not_11_out, not_12_out);
  not not_12 (not_12_out, A);
  not not_13 (not_13_out, C);
  and and_9 (and_9_out, not_13_out, not_14_out);
  not not_14 (not_14_out, A);
  not not_15 (not_15_out, D);
  and and_10 (and_10_out, not_15_out, B, A);
  not not_16 (not_16_out, B);
  and and_11 (and_11_out, D, not_16_out, A);
  not not_17 (not_17_out, D);
  and and_12 (and_12_out, not_17_out, not_18_out);
  not not_18 (not_18_out, B);
  not not_19 (not_19_out, D);
  and and_13 (and_13_out, not_19_out, A);
  not not_20 (not_20_out, B);
  and and_14 (and_14_out, not_20_out, A);
  not not_21 (not_21_out, D);
  and and_15 (and_15_out, not_21_out, C);
  and and_16 (and_16_out, D, not_22_out);
  not not_22 (not_22_out, C);
  not not_23 (not_23_out, D);
  not not_24 (not_24_out, C);
  and and_17 (and_17_out, not_23_out, not_24_out, not_25_out);
  not not_25 (not_25_out, A);
  not not_26 (not_26_out, C);
  and and_18 (and_18_out, not_26_out, B, A);
  and and_19 (and_19_out, C, not_27_out, A);
  not not_27 (not_27_out, B);
  and and_20 (and_20_out, C, B, not_28_out);
  not not_28 (not_28_out, A);
  not not_29 (not_29_out, B);
  and and_21 (and_21_out, D, not_29_out, not_30_out);
  not not_30 (not_30_out, A);
  not not_31 (not_31_out, C);
  and and_22 (and_22_out, not_31_out, not_32_out);
  not not_32 (not_32_out, A);
  and and_23 (and_23_out, B, not_33_out);
  not not_33 (not_33_out, A);
  and and_24 (and_24_out, D, B);
  and and_25 (and_25_out, D, C);
  not not_34 (not_34_out, B);
  and and_26 (and_26_out, not_34_out, not_35_out);
  not not_35 (not_35_out, A);
  not not_36 (not_36_out, D);
  and and_27 (and_27_out, not_36_out, C, not_37_out);
  not not_37 (not_37_out, B);
  and and_28 (and_28_out, C, not_38_out);
  not not_38 (not_38_out, A);
  and and_29 (and_29_out, D, not_39_out);
  not not_39 (not_39_out, C);
  and and_30 (and_30_out, D, B);
  not not_40 (not_40_out, C);
  and and_31 (and_31_out, not_40_out, B);
  and and_32 (and_32_out, B, not_41_out);
  not not_41 (not_41_out, A);
  not not_42 (not_42_out, D);
  and and_33 (and_33_out, not_42_out, C, not_43_out);
  not not_43 (not_43_out, B);
  and and_34 (and_34_out, D, not_44_out);
  not not_44 (not_44_out, C);
  and and_35 (and_35_out, D, A);
  or or_1 (b_2, and_7_out, and_8_out, and_9_out, and_10_out, and_11_out);
  or or_2 (c_2, and_12_out, and_13_out, and_14_out, and_15_out, and_16_out);
  or or_3 (d_2, and_17_out, and_18_out, and_19_out, and_20_out, and_21_out);
  or or_4 (e, and_22_out, and_23_out, and_24_out, and_25_out);
  or or_5 (f, and_26_out, and_27_out, and_28_out, and_29_out, and_30_out);
  or or_6 (g, and_31_out, and_32_out, and_33_out, and_34_out, and_35_out);
  or or_7 (a_2, and_1_out, and_2_out, and_3_out, and_4_out, and_5_out, and_6_out);
endmodule
